# Fritzing sketch schematic (saved by Fritzing 0.7.10b)
breadboards: 1

parts:
  S1 = Pushbutton [package="[THT]"]
  S2 = Pushbutton [package="[THT]"]
  S3 = Pushbutton [package="[THT]"]
  S4 = Pushbutton [package="[THT]"]
  LCD1 = LCD screen
  Arduino1 = Arduino
  R1 = Resistor [tolerance=±5% resistance=330 package=THT]
  R2 = Resistor [tolerance=±5% resistance=330 package=THT]
  R3 = Resistor [tolerance=±5% resistance=330 package=THT]
  R4 = Resistor [tolerance=±5% resistance=330 package=THT]

nets:
  N1: S1.Pin_1, S1.Pin_2, S2.Pin_1, S2.Pin_2, S3.Pin_1, S3.Pin_2, S4.Pin_1, S4.Pin_2, Arduino1.+5V
  N2: S1.Pin_3, S1.Pin_4, Arduino1.A0, R1.Pin_1
  N3: S2.Pin_3, S2.Pin_4, Arduino1.A1, R2.Pin_1
  N4: S3.Pin_3, S3.Pin_4, Arduino1.A2, R3.Pin_1
  N5: S4.Pin_3, S4.Pin_4, Arduino1.A4, R4.Pin_1
  VSS: LCD1.VSS, LCD1.V0, LCD1.R/W, LCD1.LED-, Arduino1.GND, R1.Pin_0, R2.Pin_0, R3.Pin_0, R4.Pin_0
  VDD: LCD1.VDD, LCD1.LED+, Arduino1.3V3
  N6: LCD1.RS, Arduino1.D2
  N7: LCD1.E, Arduino1.D3
  N8: LCD1.DB4, Arduino1.D10
  N9: LCD1.DB5, Arduino1.D11
  N10: LCD1.DB6, Arduino1.D12
  N11: LCD1.DB7, Arduino1.D13
